# Fritzing sketch Arduino_SpectrumAnalyzer_Schematics (saved by Fritzing 0.9.3b)

parts:
  ARDUINO_NANO = Arduino Nano (Rev3.0)
  MAX7219_32X8 = LED Matrix - Serial Interface - Red/Green/Blue
  Part8 = LED Matrix - Serial Interface - Red/Green/Blue  # not connected
  Part9 = LED Matrix - Serial Interface - Red/Green/Blue  # not connected
  Part10 = LED Matrix - Serial Interface - Red/Green/Blue  # not connected
  BUTTON_A = Round Pushbutton
  BUTTON_B = Round Pushbutton
  DC_5V = Power Jack [package=power_jack_pth_lock]
  D1 = Zener Diode [part_number=1N4732A breakdown_voltage=3.6V package="300 mil [THT]"]
  TRS1 = Audio Jack (TRS) 3.5mm [package="4Ucon 08780 [THT]"]
  C1 = Ceramic Capacitor [capacitance=100nF package="200 mil [THT, multilayer]"]
  C2 = Ceramic Capacitor [capacitance=100nF package="200 mil [THT, multilayer]"]
  R1 = Resistor [tolerance=±1% resistance=4.7k package=THT]
  R2 = Resistor [tolerance=±1% resistance=4.7k package=THT]
  R3 = Resistor [tolerance=±1% resistance=100k package=THT]
  C3 = Ceramic Capacitor [capacitance=22nF package="200 mil [THT, multilayer]"]
  R4 = Resistor [tolerance=±1% resistance=100k package=THT]  # not connected
  R5 = Resistor [tolerance=±1% resistance=4.7k package=THT]  # not connected
  R6 = Resistor [tolerance=±1% resistance=10k package=THT]

nets:
  GND: ARDUINO_NANO.GND, MAX7219_32X8.GND, DC_5V.GND
  N1: ARDUINO_NANO.D2, BUTTON_A.leg0
  N2: ARDUINO_NANO.D3, BUTTON_B.leg0
  N3: ARDUINO_NANO.D10, MAX7219_32X8.CS
  N4: ARDUINO_NANO.D11/MOSI, MAX7219_32X8.MOSI
  N5: ARDUINO_NANO.5V, D1.cathode
  N6: ARDUINO_NANO.A0, C3.1, R6.Pin_0
  N7: ARDUINO_NANO.D13/SCK, MAX7219_32X8.SCK
  N8: MAX7219_32X8.VCC, BUTTON_A.leg1, BUTTON_B.leg1, DC_5V.PWR, D1.anode
  N9: TRS1.Sleeve, R3.Pin_1, R6.Pin_1
  N10: TRS1.Ring, C1.0
  N11: TRS1.Tip, C2.1
  N12: C1.1, R1.Pin_0
  N13: C2.0, R2.Pin_0
  N14: R1.Pin_1, R2.Pin_1, R3.Pin_0, C3.0

custom parts:
  LED Matrix - Serial Interface - Red/Green/Blue: Description: This is a large sized RGB LED Matrix with a backpack that has been designed to take SPI serial input and display any graphics you pass it. All the refreshing and communication control is taken care of by the backpack. It's even reprogrammable! 7 software selectable colors are available! Unit comes with a Red/Green/Blue LED Matrix assembled with a RGB Matrix Backpack Controller.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
  Round Pushbutton: A generic pushbutton.
  Round Pushbutton: A generic pushbutton.
  Power Jack: Power Jack This is the standard 5.5mm barrel jack for power. The PTH is the most common, proven, reliable, footprint. All others are experimental. The Slot footprint only works if the mill layer is transmitted to the PCB fab house so be warned. Spark Fun Electronics SKU : PRT-00119. Mating wall wart : TOL-00298 (and others)
